// Logisim project 1-Bit ALU.circ as structural Verilog: 1 circuit, main circuit 1-Bit ALU
module _1_Bit_ALU (
  input  Subtract,
  input  Carry_In,
  input  [2:0] Operation,
  input  A,
  input  B,
  output Result,
  output Carry_Out
);

  wire adder_1_out, AND_out, NAND_out, NOR_out, OR_out, shifter_1_out, shifter_2_out, XOR_2_out, xor_out;

  xor \xor  (xor_out, Subtract, B);
  and AND (AND_out, A, B);
  or OR (OR_out, A, B);
  nand NAND (NAND_out, A, B);
  nor NOR (NOR_out, A, B);
  xor XOR_2 (XOR_2_out, A, B);
  Adder #(.width(1)) adder_1 (.a(A), .b(xor_out), .out(adder_1_out), .cin(Carry_In), .cout(Carry_Out));
  Shifter #(.width(1)) shifter_1 (.in(A), .\dist (B), .out(shifter_1_out));
  Shifter #(.width(1), .shift("lr")) shifter_2 (.in(A), .\dist (B), .out(shifter_2_out));
  Multiplexer #(.select(3), .enable("false")) multiplexer_1 (
    .in0(AND_out), .in1(OR_out), .in2(NAND_out), .in3(NOR_out), .in4(XOR_2_out), .in5(adder_1_out),
    .in6(shifter_1_out), .in7(shifter_2_out), .out(Result), .sel(Operation));

  // Notes on the sheet:
  //   Logical Left Shift
  //   Logical Right Shift
  //   1-Bit ALU
  //   Saeb K. H. Naser
  //   In designing my ALU, I aim to support 9 fundamental operations
  //   AND
  //   OR
  //   NAND
  //   NOR
  //   XOR
  //   Addition
  //   Subtraction
  //   Shift Right Logical
  //   Shift Left Logical
endmodule
