// Logisim project 32-Bit ALU.circ as structural Verilog: 2 circuits, main circuit 1-Bit ALU
module _1_Bit_ALU (
  input  Subtract,
  input  Carry_In,
  input  [2:0] Operation,
  input  A,
  input  B,
  output Result,
  output Carry_Out
);

  wire adder_1_out, AND_out, NAND_out, NOR_out, OR_out, shifter_1_out, shifter_2_out, XOR_2_out, xor_out;

  xor \xor  (xor_out, Subtract, B);
  and AND (AND_out, A, B);
  or OR (OR_out, A, B);
  nand NAND (NAND_out, A, B);
  nor NOR (NOR_out, A, B);
  xor XOR_2 (XOR_2_out, A, B);
  Adder #(.width(1)) adder_1 (.a(A), .b(xor_out), .out(adder_1_out), .cin(Carry_In), .cout(Carry_Out));
  Shifter #(.width(1)) shifter_1 (.in(A), .\dist (B), .out(shifter_1_out));
  Shifter #(.width(1), .shift("lr")) shifter_2 (.in(A), .\dist (B), .out(shifter_2_out));
  Multiplexer #(.select(3), .enable("false")) multiplexer_1 (
    .in0(AND_out), .in1(OR_out), .in2(NAND_out), .in3(NOR_out), .in4(XOR_2_out), .in5(adder_1_out),
    .in6(shifter_1_out), .in7(shifter_2_out), .out(Result), .sel(Operation));

  // Notes on the sheet:
  //   Logical Left Shift
  //   Logical Right Shift
  //   1-Bit ALU
  //   Saeb K. H. Naser
  //   In designing my ALU, I aim to support 9 fundamental operations
  //   AND
  //   OR
  //   NAND
  //   NOR
  //   XOR
  //   Addition
  //   Subtraction
  //   Shift Right Logical
  //   Shift Left Logical
endmodule

module _32_Bit_ALU (
  input  Subtract,
  input  [2:0] Operation,
  input  [31:0] A,
  input  [31:0] B,
  output [31:0] Result
);

  wire n1_bit_alu_1_carry_out, n1_bit_alu_2_carry_out, n1_bit_alu_3_carry_out, n1_bit_alu_4_carry_out,
       n1_bit_alu_5_carry_out, n1_bit_alu_6_carry_out, n1_bit_alu_7_carry_out, n1_bit_alu_8_carry_out,
       n1_bit_alu_9_carry_out, n1_bit_alu_10_carry_out, n1_bit_alu_11_carry_out, n1_bit_alu_12_carry_out,
       n1_bit_alu_13_carry_out, n1_bit_alu_14_carry_out, n1_bit_alu_15_carry_out, n1_bit_alu_16_carry_out,
       n1_bit_alu_17_carry_out, n1_bit_alu_18_carry_out, n1_bit_alu_19_carry_out, n1_bit_alu_20_carry_out,
       n1_bit_alu_21_carry_out, n1_bit_alu_22_carry_out, n1_bit_alu_23_carry_out, n1_bit_alu_24_carry_out,
       n1_bit_alu_25_carry_out, n1_bit_alu_26_carry_out, n1_bit_alu_27_carry_out, n1_bit_alu_28_carry_out,
       n1_bit_alu_29_carry_out, n1_bit_alu_30_carry_out, n1_bit_alu_31_carry_out;

  _1_Bit_ALU u_1_bit_alu_1 (
    .A(A[0]), .B(B[0]), .Result(Result[0]), .Subtract(Subtract), .Carry_In(Subtract), .Operation(Operation),
    .Carry_Out(n1_bit_alu_1_carry_out));
  _1_Bit_ALU u_1_bit_alu_2 (
    .A(A[1]), .B(B[1]), .Result(Result[1]), .Subtract(Subtract), .Carry_In(n1_bit_alu_1_carry_out),
    .Operation(Operation), .Carry_Out(n1_bit_alu_2_carry_out));
  _1_Bit_ALU u_1_bit_alu_3 (
    .A(A[2]), .B(B[2]), .Result(Result[2]), .Subtract(Subtract), .Carry_In(n1_bit_alu_2_carry_out),
    .Operation(Operation), .Carry_Out(n1_bit_alu_3_carry_out));
  _1_Bit_ALU u_1_bit_alu_4 (
    .A(A[3]), .B(B[3]), .Result(Result[3]), .Subtract(Subtract), .Carry_In(n1_bit_alu_3_carry_out),
    .Operation(Operation), .Carry_Out(n1_bit_alu_4_carry_out));
  _1_Bit_ALU u_1_bit_alu_5 (
    .A(A[4]), .B(B[4]), .Result(Result[4]), .Subtract(Subtract), .Carry_In(n1_bit_alu_4_carry_out),
    .Operation(Operation), .Carry_Out(n1_bit_alu_5_carry_out));
  _1_Bit_ALU u_1_bit_alu_6 (
    .A(A[5]), .B(B[5]), .Result(Result[5]), .Subtract(Subtract), .Carry_In(n1_bit_alu_5_carry_out),
    .Operation(Operation), .Carry_Out(n1_bit_alu_6_carry_out));
  _1_Bit_ALU u_1_bit_alu_7 (
    .A(A[6]), .B(B[6]), .Result(Result[6]), .Subtract(Subtract), .Carry_In(n1_bit_alu_6_carry_out),
    .Operation(Operation), .Carry_Out(n1_bit_alu_7_carry_out));
  _1_Bit_ALU u_1_bit_alu_8 (
    .A(A[7]), .B(B[7]), .Result(Result[7]), .Subtract(Subtract), .Carry_In(n1_bit_alu_7_carry_out),
    .Operation(Operation), .Carry_Out(n1_bit_alu_8_carry_out));
  _1_Bit_ALU u_1_bit_alu_9 (
    .A(A[8]), .B(B[8]), .Result(Result[8]), .Subtract(Subtract), .Carry_In(n1_bit_alu_8_carry_out),
    .Operation(Operation), .Carry_Out(n1_bit_alu_9_carry_out));
  _1_Bit_ALU u_1_bit_alu_10 (
    .A(A[9]), .B(B[9]), .Result(Result[9]), .Subtract(Subtract), .Carry_In(n1_bit_alu_9_carry_out),
    .Operation(Operation), .Carry_Out(n1_bit_alu_10_carry_out));
  _1_Bit_ALU u_1_bit_alu_11 (
    .A(A[10]), .B(B[10]), .Result(Result[10]), .Subtract(Subtract), .Carry_In(n1_bit_alu_10_carry_out),
    .Operation(Operation), .Carry_Out(n1_bit_alu_11_carry_out));
  _1_Bit_ALU u_1_bit_alu_12 (
    .A(A[11]), .B(B[11]), .Result(Result[11]), .Subtract(Subtract), .Carry_In(n1_bit_alu_11_carry_out),
    .Operation(Operation), .Carry_Out(n1_bit_alu_12_carry_out));
  _1_Bit_ALU u_1_bit_alu_13 (
    .A(A[12]), .B(B[12]), .Result(Result[12]), .Subtract(Subtract), .Carry_In(n1_bit_alu_12_carry_out),
    .Operation(Operation), .Carry_Out(n1_bit_alu_13_carry_out));
  _1_Bit_ALU u_1_bit_alu_14 (
    .A(A[13]), .B(B[13]), .Result(Result[13]), .Subtract(Subtract), .Carry_In(n1_bit_alu_13_carry_out),
    .Operation(Operation), .Carry_Out(n1_bit_alu_14_carry_out));
  _1_Bit_ALU u_1_bit_alu_15 (
    .A(A[14]), .B(B[14]), .Result(Result[14]), .Subtract(Subtract), .Carry_In(n1_bit_alu_14_carry_out),
    .Operation(Operation), .Carry_Out(n1_bit_alu_15_carry_out));
  _1_Bit_ALU u_1_bit_alu_16 (
    .A(A[15]), .B(B[15]), .Result(Result[15]), .Subtract(Subtract), .Carry_In(n1_bit_alu_15_carry_out),
    .Operation(Operation), .Carry_Out(n1_bit_alu_16_carry_out));
  _1_Bit_ALU u_1_bit_alu_17 (
    .A(A[16]), .B(B[16]), .Result(Result[16]), .Subtract(Subtract), .Carry_In(n1_bit_alu_16_carry_out),
    .Operation(Operation), .Carry_Out(n1_bit_alu_17_carry_out));
  _1_Bit_ALU u_1_bit_alu_18 (
    .A(A[17]), .B(B[17]), .Result(Result[17]), .Subtract(Subtract), .Carry_In(n1_bit_alu_17_carry_out),
    .Operation(Operation), .Carry_Out(n1_bit_alu_18_carry_out));
  _1_Bit_ALU u_1_bit_alu_19 (
    .A(A[18]), .B(B[18]), .Result(Result[18]), .Subtract(Subtract), .Carry_In(n1_bit_alu_18_carry_out),
    .Operation(Operation), .Carry_Out(n1_bit_alu_19_carry_out));
  _1_Bit_ALU u_1_bit_alu_20 (
    .A(A[19]), .B(B[19]), .Result(Result[19]), .Subtract(Subtract), .Carry_In(n1_bit_alu_19_carry_out),
    .Operation(Operation), .Carry_Out(n1_bit_alu_20_carry_out));
  _1_Bit_ALU u_1_bit_alu_21 (
    .A(A[20]), .B(B[20]), .Result(Result[20]), .Subtract(Subtract), .Carry_In(n1_bit_alu_20_carry_out),
    .Operation(Operation), .Carry_Out(n1_bit_alu_21_carry_out));
  _1_Bit_ALU u_1_bit_alu_22 (
    .A(A[21]), .B(B[21]), .Result(Result[21]), .Subtract(Subtract), .Carry_In(n1_bit_alu_21_carry_out),
    .Operation(Operation), .Carry_Out(n1_bit_alu_22_carry_out));
  _1_Bit_ALU u_1_bit_alu_23 (
    .A(A[22]), .B(B[22]), .Result(Result[22]), .Subtract(Subtract), .Carry_In(n1_bit_alu_22_carry_out),
    .Operation(Operation), .Carry_Out(n1_bit_alu_23_carry_out));
  _1_Bit_ALU u_1_bit_alu_24 (
    .A(A[23]), .B(B[23]), .Result(Result[23]), .Subtract(Subtract), .Carry_In(n1_bit_alu_23_carry_out),
    .Operation(Operation), .Carry_Out(n1_bit_alu_24_carry_out));
  _1_Bit_ALU u_1_bit_alu_25 (
    .A(A[24]), .B(B[24]), .Result(Result[24]), .Subtract(Subtract), .Carry_In(n1_bit_alu_24_carry_out),
    .Operation(Operation), .Carry_Out(n1_bit_alu_25_carry_out));
  _1_Bit_ALU u_1_bit_alu_26 (
    .A(A[25]), .B(B[25]), .Result(Result[25]), .Subtract(Subtract), .Carry_In(n1_bit_alu_25_carry_out),
    .Operation(Operation), .Carry_Out(n1_bit_alu_26_carry_out));
  _1_Bit_ALU u_1_bit_alu_27 (
    .A(A[26]), .B(B[26]), .Result(Result[26]), .Subtract(Subtract), .Carry_In(n1_bit_alu_26_carry_out),
    .Operation(Operation), .Carry_Out(n1_bit_alu_27_carry_out));
  _1_Bit_ALU u_1_bit_alu_28 (
    .A(A[27]), .B(B[27]), .Result(Result[27]), .Subtract(Subtract), .Carry_In(n1_bit_alu_27_carry_out),
    .Operation(Operation), .Carry_Out(n1_bit_alu_28_carry_out));
  _1_Bit_ALU u_1_bit_alu_29 (
    .A(A[28]), .B(B[28]), .Result(Result[28]), .Subtract(Subtract), .Carry_In(n1_bit_alu_28_carry_out),
    .Operation(Operation), .Carry_Out(n1_bit_alu_29_carry_out));
  _1_Bit_ALU u_1_bit_alu_30 (
    .A(A[29]), .B(B[29]), .Result(Result[29]), .Subtract(Subtract), .Carry_In(n1_bit_alu_29_carry_out),
    .Operation(Operation), .Carry_Out(n1_bit_alu_30_carry_out));
  _1_Bit_ALU u_1_bit_alu_31 (
    .A(A[30]), .B(B[30]), .Result(Result[30]), .Subtract(Subtract), .Carry_In(n1_bit_alu_30_carry_out),
    .Operation(Operation), .Carry_Out(n1_bit_alu_31_carry_out));
  _1_Bit_ALU u_1_bit_alu_32 (
    .A(A[31]), .B(B[31]), .Result(Result[31]), .Subtract(Subtract), .Carry_In(n1_bit_alu_31_carry_out),
    .Operation(Operation));  // open: Carry_Out

  // Notes on the sheet:
  //   32-Bit ALU
  //   AND
  //   OR
  //   NAND
  //   NOR
  //   Saeb K. H. Naser
  //   In designing my ALU, I aim to support 9 fundamental operations
  //   000
  //   001
  //   010
  //   011
  //   100
  //   XOR
  //   Addition
  //   101
  //   Subtraction
  //   110
  //   Shift Right Logical
  //   Shift Left Logical
  //   111
endmodule
